# Fritzing sketch amplified_speaker (saved by Fritzing 0.8.3b)
breadboards: 1

parts:
  Part1 = Arduino Leonardo (Rev3b)
  SPKR1 = Loudspeaker
  R1 = Trimmer Potentiometer [maximum_resistance=10kΩ package=THT]
  U2 = LM386 [package=dip08]
  C1 = Electrolytic Capacitor [capacitance=220µF voltage=16V package="100 mil [THT, electrolytic]"]

nets:
  N1: Part1.D6_PWM/A7, R1.leg2
  5V: Part1.5V, U2.V+
  GND: Part1.GND, SPKR1.pin1, R1.leg1, U2.-IN, U2.V-
  N2: SPKR1.pin2, C1.-
  N3: R1.wiper, U2.+IN
  N4: U2.OUT, C1.+
