# Fritzing sketch simple_speaker (saved by Fritzing 0.8.3b)
breadboards: 1

parts:
  Part1 = Arduino Leonardo (Rev3b)
  SPKR1 = Loudspeaker
  R1 = Resistor [tolerance=±5% resistance=100 package=THT]

nets:
  N1: Part1.D6_PWM/A7, R1.Pin_1
  N2: Part1.GND, SPKR1.pin1
  N3: SPKR1.pin2, R1.Pin_0
